// Logisim project circuito-ULA.circ as structural Verilog: 1 circuit, main circuit main
module main (
  input  Opt1,
  input  Opt0,
  input  in_3,
  input  in_4,
  input  Resetar_tudo,
  input  Binvert,
  output X4,
  output X3,
  output X2,
  output X1,
  output X0
);

  wire and_1_out, and_2_out, and_3_out, and_4_out, and_5_out, and_6_out, and_7_out, and_8_out, and_9_out,
       and_10_out, and_11_out, Cin_Cout_q, Clock__Clique_10_vezes_out, d_ff_1_q, d_ff_2_q, d_ff_3_q,
       d_ff_4_q, d_ff_5_q, d_ff_6_q, d_ff_7_q, d_ff_8_q, d_ff_9_q, d_ff_10_q, d_ff_10_qn, not_1_out,
       not_2_out, not_3_out, not_4_out, or_1_out, or_2_out, or_3_out, or_4_out, or_5_out, or_6_out,
       xor_1_out, xor_2_out;

  D_Flip_Flop Cin_Cout (
    .clk(Clock__Clique_10_vezes_out), .D(or_2_out), .Q(Cin_Cout_q), .reset(Resetar_tudo));  // open: Qn, preset, en
  xor xor_1 (xor_1_out, d_ff_9_q, or_3_out);
  and and_1 (and_1_out, or_3_out, d_ff_9_q);
  or or_1 (or_1_out, or_3_out, d_ff_9_q);
  Clock Clock__Clique_10_vezes (.out(Clock__Clique_10_vezes_out));
  xor xor_2 (xor_2_out, xor_1_out, Cin_Cout_q);
  and and_2 (and_2_out, Cin_Cout_q, xor_1_out);
  and and_3 (and_3_out, d_ff_9_q, or_3_out);
  D_Flip_Flop d_ff_1 (
    .clk(Clock__Clique_10_vezes_out), .D(in_3), .Q(d_ff_1_q), .reset(Resetar_tudo));  // open: Qn, preset, en
  D_Flip_Flop d_ff_2 (
    .clk(Clock__Clique_10_vezes_out), .D(in_4), .Q(d_ff_2_q), .reset(Resetar_tudo));  // open: Qn, preset, en
  or or_2 (or_2_out, and_2_out, and_3_out);
  D_Flip_Flop d_ff_3 (
    .clk(Clock__Clique_10_vezes_out), .D(d_ff_1_q), .Q(d_ff_3_q), .reset(Resetar_tudo));  // open: Qn, preset, en
  D_Flip_Flop d_ff_4 (
    .clk(Clock__Clique_10_vezes_out), .D(d_ff_2_q), .Q(d_ff_4_q), .reset(Resetar_tudo));  // open: Qn, preset, en
  D_Flip_Flop d_ff_5 (
    .clk(Clock__Clique_10_vezes_out), .D(d_ff_3_q), .Q(d_ff_5_q), .reset(Resetar_tudo));  // open: Qn, preset, en
  D_Flip_Flop d_ff_6 (
    .clk(Clock__Clique_10_vezes_out), .D(d_ff_4_q), .Q(d_ff_6_q), .reset(Resetar_tudo));  // open: Qn, preset, en
  not not_1 (not_1_out, Binvert);
  D_Flip_Flop d_ff_7 (
    .clk(Clock__Clique_10_vezes_out), .D(d_ff_5_q), .Q(d_ff_7_q), .reset(Resetar_tudo));  // open: Qn, preset, en
  D_Flip_Flop d_ff_8 (
    .clk(Clock__Clique_10_vezes_out), .D(d_ff_6_q), .Q(d_ff_8_q), .reset(Resetar_tudo));  // open: Qn, preset, en
  and and_4 (and_4_out, d_ff_10_qn, Binvert);
  and and_5 (and_5_out, not_1_out, d_ff_10_q);
  D_Flip_Flop d_ff_9 (
    .clk(Clock__Clique_10_vezes_out), .D(d_ff_7_q), .Q(d_ff_9_q), .reset(Resetar_tudo));  // open: Qn, preset, en
  D_Flip_Flop d_ff_10 (
    .clk(Clock__Clique_10_vezes_out), .D(d_ff_8_q), .Q(d_ff_10_q), .Qn(d_ff_10_qn), .reset(Resetar_tudo));  // open: preset, en
  or or_3 (or_3_out, and_4_out, and_5_out);
  D_Flip_Flop d_ff_11 (
    .clk(Clock__Clique_10_vezes_out), .D(or_6_out), .Q(X4), .reset(Resetar_tudo));  // open: Qn, preset, en
  not not_2 (not_2_out, Opt0);
  D_Flip_Flop d_ff_12 (.clk(Clock__Clique_10_vezes_out), .D(X4), .Q(X3), .reset(Resetar_tudo));  // open: Qn, preset, en
  not not_3 (not_3_out, Opt0);
  D_Flip_Flop d_ff_13 (.clk(Clock__Clique_10_vezes_out), .D(X3), .Q(X2), .reset(Resetar_tudo));  // open: Qn, preset, en
  and and_6 (and_6_out, not_3_out, and_1_out);
  and and_7 (and_7_out, Opt0, or_1_out);
  and and_8 (and_8_out, not_2_out, xor_2_out);
  buf and_9 (and_9_out, Opt0);  // AND_Gate
  or or_4 (or_4_out, and_6_out, and_7_out);
  or or_5 (or_5_out, and_8_out, and_9_out);
  D_Flip_Flop d_ff_14 (.clk(Clock__Clique_10_vezes_out), .D(X2), .Q(X1), .reset(Resetar_tudo));  // open: Qn, preset, en
  D_Flip_Flop d_ff_15 (.clk(Clock__Clique_10_vezes_out), .D(X1), .Q(X0), .reset(Resetar_tudo));  // open: Qn, preset, en
  not not_4 (not_4_out, Opt1);
  and and_10 (and_10_out, not_4_out, or_4_out);
  and and_11 (and_11_out, Opt1, or_5_out);
  or or_6 (or_6_out, and_10_out, and_11_out);

  // Notes on the sheet:
  //   Soma/Subtracao
  //   Mude para 1 em subtracoes
  //   AND
  //   OR
  //   Entrada A
  //   Entrada B
  //   MUX 2-1
  //   Mude para 1 em subtracoes
  //   00 = AND, 01 = OR, 10 = Soma/Sub.
  //   Resultado Final
  //   MUX 4-1
endmodule
